# Fritzing sketch lab1 (saved by Fritzing 0.8.3b)
breadboards: 1

parts:
  D1 = LED_BARGRAPH_10 [package=led_bargaph_10]
  IC1 = IC, DIP package, 14 pins [chip_label=7408/7432]

nets:
  N1: D1.A_A, IC1.pin1
  N2: D1.B_A, D1.I_C, IC1.pin2
  N3: D1.C_A, IC1.pin3
