# Fritzing sketch lab4 (saved by Fritzing 0.8.3b)
breadboards: 1

parts:
  U1 = 555 Timer [package="DIP8 [THT]"]
  D1 = LED_BARGRAPH_10 [package=led_bargaph_10]
  R1 = Resistor [tolerance=±5% resistance=220 package=THT]
  R2 = Resistor [tolerance=±5% resistance=220 package=THT]
  IC1 = IC, DIP package, 14 pins [chip_label=7404]
  IC2 = IC, DIP package, 14 pins [chip_label=7432]
  IC3 = IC, DIP package, 14 pins [chip_label=74164]
  C1 = Ceramic Capacitor [capacitance=100nF package="100 mil [THT, multilayer]"]

nets:
  N1: U1.Ground, IC1.pin7, IC2.pin7, IC3.pin7, C1.1
  N2: U1.Trigger, U1.Threshold, R2.Pin_0, C1.0
  N3: U1.Output, IC1.pin1
  N4: U1.Discharge, R1.Pin_0, R2.Pin_1
  N5: U1.Vcc_Supply_Voltage, R1.Pin_1, IC1.pin14, IC2.pin14, IC3.pin9, IC3.pin14
  N6: D1.A_A, IC2.pin5, IC3.pin3
  N7: D1.B_A, IC2.pin2, IC3.pin4
  N8: D1.C_A, IC2.pin1, IC3.pin5
  N9: D1.D_A, IC3.pin6
  N10: IC1.pin2, IC1.pin3
  N11: IC1.pin4, IC3.pin8
  N12: IC1.pin5, IC2.pin6
  N13: IC1.pin6, IC3.pin1, IC3.pin2
  N14: IC2.pin3, IC2.pin4
